# Fritzing sketch Fritzing2 (saved by Fritzing 0.9.3b)
breadboards: 2

parts:
  LCD1 = TFT 1.8 inch 160x128 w SD
  M1 = BluePill
  Part1 = Adafruit BME280

nets:
  5V: LCD1.pin_1, M1.5V, Part1.VIN
  GND: LCD1.pin2, M1.GND, Part1.GND
  N1: LCD1.pin3, M1.A2
  N2: LCD1.pin4, M1.A4
  N3: LCD1.pin_5, M1.A3
  N4: LCD1.pin_6, M1.A7
  N5: LCD1.pin_7, M1.A5
  N6: LCD1.pin_8, M1.3V3
  N7: M1.B6, Part1.SCK/SCL
  N8: M1.B7, Part1.SDI/SDA

custom parts:
  TFT 1.8 inch 160x128 w SD: This is a generic 1.8 tft spi lcd display available on ebay and others. The 1.8" display has 128x160 color pixels.
  BluePill: Generic ebay blue pill STM32F103C8 "Blue pill" CPU module. Arm Cortex M3 128KB flash (usually) 20kb ram, RTC on board. Supported by the Arduino IDE for programming. As cheap as an Arduino nano but with more power and memory.
  Adafruit BME280: Bosch has stepped up their game with their new BME280 sensor, an environmental sensor with temperature, barometric pressure and humidity! This sensor is great for all sorts of weather/environmental sensing and can even be used in both I2C and SPI! This precision sensor from Bosch is the best low-cost sensing solution for measuring humidity with ±3% accuracy, barometric pressure with ±1 hPa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
