# Fritzing sketch fritzing (saved by Fritzing 0.9.3b)
circuit board: 8.559cm x 6.30825cm
breadboards: 1

parts:
  LCD = TFT 1.8 inch 160x128 w SD
  Bmp280 = Adafruit BME280
  Programmer = Header 6 [package=molex-1x6_lock]
  Part1 = BluePill

nets:
  N1: LCD.pin_1, Part1.3V31
  N2: LCD.pin2, Part1.A5
  N3: LCD.pin3, Part1.A7
  N4: LCD.pin4, Part1.A3
  N5: LCD.pin_5, Part1.A4
  N6: LCD.pin_6, Part1.A2
  GND: LCD.pin_7, Bmp280.GND, Programmer.1, Part1.GND3
  VIN: LCD.pin_8, Bmp280.VIN, Programmer.3, Part1.5V
  N7: Bmp280.SCK/SCL, Part1.B6
  N8: Bmp280.SDI/SDA, Part1.B7
  N9: Programmer.4, Part1.A10
  N10: Programmer.5, Part1.A9

custom parts:
  TFT 1.8 inch 160x128 w SD: This is a generic 1.8 tft spi lcd display available on ebay and others. The 1.8" display has 128x160 color pixels.
  Adafruit BME280: Bosch has stepped up their game with their new BME280 sensor, an environmental sensor with temperature, barometric pressure and humidity! This sensor is great for all sorts of weather/environmental sensing and can even be used in both I2C and SPI! This precision sensor from Bosch is the best low-cost sensing solution for measuring humidity with ±3% accuracy, barometric pressure with ±1 hPa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
