# Fritzing sketch stm32st7735 (saved by Fritzing 0.9.3b)
circuit board: 8.559cm x 6.30825cm
breadboards: 1

parts:
  Programmer = Header 6 [package=molex-1x6_lock]
  Part1 = BluePill
  LCD = TFT 1.8 inch 160x128 w SD

nets (from the pcb view):
  N1: Programmer.1, Part1.GND3
  N2: Programmer.3, Part1.3V31, LCD.pin_1, LCD.pin_8
  N3: Programmer.4, Part1.A10
  N4: Programmer.5, Part1.A9
  N5: Part1.A3, LCD.pin_5
  N6: Part1.A5, LCD.pin_7
  N7: Part1.A7, LCD.pin_6
  N8: Part1.A2, LCD.pin3

notes:
  Ishan

custom parts:
  TFT 1.8 inch 160x128 w SD: This is a generic 1.8 tft spi lcd display available on ebay and others. The 1.8" display has 128x160 color pixels.
